// Logisim project logisim.circ as structural Verilog: 4 circuits, main circuit main
module main (
);

  wire button_1_out, button_2_out, button_3_out, button_4_out, button_5_out, button_6_out, button_7_out,
       button_8_out, button_9_out, button_10_out, button_11_out, button_12_out, button_13_out, button_14_out,
       button_15_out, button_16_out, button_17_out, button_18_out, controller_1_a11_2, controller_1_a12_2,
       controller_1_a13_2, controller_1_a21_2, controller_1_a22_2, controller_1_a23_2, controller_1_a31_2,
       controller_1_a32_2, controller_1_a33_2, controller_1_b11_2, controller_1_b12_2, controller_1_b13_2,
       controller_1_b21_2, controller_1_b22_2, controller_1_b23_2, controller_1_b31_2, controller_1_b32_2,
       controller_1_b33_2, controller_1_wa, controller_1_wb;

  Button button_1 (.out(button_1_out));
  Button button_2 (.out(button_2_out));
  Button button_3 (.out(button_3_out));
  Button button_4 (.out(button_4_out));
  Button button_5 (.out(button_5_out));
  Button button_6 (.out(button_6_out));
  Button button_7 (.out(button_7_out));
  Button button_8 (.out(button_8_out));
  Button button_9 (.out(button_9_out));
  Button button_10 (.out(button_10_out));
  Button button_11 (.out(button_11_out));
  Button button_12 (.out(button_12_out));
  Button button_13 (.out(button_13_out));
  Button button_14 (.out(button_14_out));
  Button button_15 (.out(button_15_out));
  Button button_16 (.out(button_16_out));
  Button button_17 (.out(button_17_out));
  Button button_18 (.out(button_18_out));
  controller controller_1 (
    .a11(button_1_out), .a12(button_2_out), .a13(button_13_out), .a21(button_3_out), .a22(button_4_out),
    .a23(button_14_out), .a31(button_6_out), .a32(button_5_out), .a33(button_15_out), .b11(button_7_out),
    .b12(button_8_out), .b13(button_16_out), .b21(button_10_out), .b22(button_9_out), .b23(button_17_out),
    .b31(button_11_out), .b32(button_12_out), .b33(button_18_out), .A11_2(controller_1_a11_2),
    .A12_2(controller_1_a12_2), .A13_2(controller_1_a13_2), .A21_2(controller_1_a21_2),
    .A22_2(controller_1_a22_2), .A23_2(controller_1_a23_2), .WA(controller_1_wa), .A31_2(controller_1_a31_2),
    .A32_2(controller_1_a32_2), .A33_2(controller_1_a33_2), .B11_2(controller_1_b11_2),
    .B12_2(controller_1_b12_2), .B13_2(controller_1_b13_2), .B21_2(controller_1_b21_2),
    .B22_2(controller_1_b22_2), .B23_2(controller_1_b23_2), .WB(controller_1_wb), .B31_2(controller_1_b31_2),
    .B32_2(controller_1_b32_2), .B33_2(controller_1_b33_2));
  LED led_1 (.in(controller_1_wb));
  LED led_2 (.in(controller_1_wa));
  LED led_3 (.in(controller_1_b11_2));
  LED led_4 (.in(controller_1_a11_2));
  LED led_5 (.in(controller_1_b21_2));
  LED led_6 (.in(controller_1_a21_2));
  LED led_7 (.in(controller_1_b31_2));
  LED led_8 (.in(controller_1_a31_2));
  LED led_9 (.in(controller_1_a12_2));
  LED led_10 (.in(controller_1_b12_2));
  LED led_11 (.in(controller_1_a22_2));
  LED led_12 (.in(controller_1_b22_2));
  LED led_13 (.in(controller_1_b32_2));
  LED led_14 (.in(controller_1_a32_2));
  LED led_15 (.in(controller_1_a13_2));
  LED led_16 (.in(controller_1_b13_2));
  LED led_17 (.in(controller_1_a23_2));
  LED led_18 (.in(controller_1_b23_2));
  LED led_19 (.in(controller_1_a33_2));
  LED led_20 (.in(controller_1_b33_2));

  // Notes on the sheet:
  //   PLAYER
  //   1
  //   PLAYER
  //   2
  //   WINNER
  //   TIC TAC TOE
  //   GRID
endmodule

module controller (
  input  a11,
  input  a12,
  input  a13,
  input  a21,
  input  a22,
  input  a23,
  input  a31,
  input  a32,
  input  a33,
  input  b11,
  input  b12,
  input  b13,
  input  b21,
  input  b22,
  input  b23,
  input  b31,
  input  b32,
  input  b33,
  output A11_2,
  output A12_2,
  output A13_2,
  output A21_2,
  output A22_2,
  output A23_2,
  output WA,
  output A31_2,
  output A32_2,
  output A33_2,
  output B11_2,
  output B12_2,
  output B13_2,
  output B21_2,
  output B22_2,
  output B23_2,
  output WB,
  output B31_2,
  output B32_2,
  output B33_2
);

  mover mover_1 (.X(a11), .Y(b11), .O1(A11_2), .O2(B11_2));
  mover mover_2 (.X(a21), .Y(b21), .O1(A21_2), .O2(B21_2));
  mover mover_3 (.X(a31), .Y(b31), .O1(A31_2), .O2(B31_2));
  mover mover_4 (.X(a12), .Y(b12), .O1(A12_2), .O2(B12_2));
  mover mover_5 (.X(a22), .Y(b22), .O1(A22_2), .O2(B22_2));
  mover mover_6 (.X(a32), .Y(b32), .O1(A32_2), .O2(B32_2));
  mover mover_7 (.X(a13), .Y(b13), .O1(A13_2), .O2(B13_2));
  mover mover_8 (.X(a23), .Y(b23), .O1(A23_2), .O2(B23_2));
  mover mover_9 (.X(a33), .Y(b33), .O1(A33_2), .O2(B33_2));
  windetect windetect_1 (
    .a(A11_2), .b(A12_2), .c(A13_2), .d(A21_2), .e(A22_2), .f(A23_2), .g(A31_2), .h(A32_2), .i(A33_2), .W(WA));
  windetect windetect_2 (
    .a(B11_2), .b(B12_2), .c(B13_2), .d(B21_2), .e(B22_2), .f(B23_2), .g(B31_2), .h(B32_2), .i(B33_2), .W(WB));
endmodule

module mover (
  input  X,
  input  Y,
  output O1,
  output O2
);

  wire and_1_out, and_2_out, not_1_out, not_2_out;

  not not_1 (not_1_out, O2);
  not not_2 (not_2_out, O1);
  and and_1 (and_1_out, X, not_1_out);
  and and_2 (and_2_out, Y, not_2_out);
  D_Flip_Flop d_ff_1 (.clk(and_1_out), .D(and_1_out), .Q(O1));  // open: Qn, preset, en, reset
  D_Flip_Flop d_ff_2 (.clk(and_2_out), .D(and_2_out), .Q(O2));  // open: Qn, preset, en, reset
endmodule

module windetect (
  input  a,
  input  b,
  input  c,
  input  d,
  input  e,
  input  f,
  input  g,
  input  h,
  input  i,
  output W
);

  wire and_1_out, and_2_out, and_3_out, and_4_out, and_5_out, and_6_out, and_7_out, and_8_out;

  and and_1 (and_1_out, a, b, c);
  and and_2 (and_2_out, d, e, f);
  and and_3 (and_3_out, g, h, i);
  and and_4 (and_4_out, a, e, i);
  and and_5 (and_5_out, a, d, g);
  and and_6 (and_6_out, b, e, h);
  and and_7 (and_7_out, c, f, i);
  and and_8 (and_8_out, c, e, g);
  or or_1 (W, and_1_out, and_2_out, and_3_out, and_4_out, and_5_out, and_6_out, and_7_out, and_8_out);
endmodule
